// Logisim project main.circ as structural Verilog: 4 circuits, main circuit main
module main (
  input  in_1,
  input  [15:0] in_2,
  input  in_3,
  input  in_4,
  output [15:0] out_5
);

  wire clock_1_out;

  Clock clock_1 (.out(clock_1_out));
  counter counter_1 (.clk(clock_1_out), .enable_chip(in_1), .in_3(in_2), .reset(in_4), .in_5(in_3), .out_6(out_5));
endmodule

module high_register (
  input  in_1,
  input  [7:0] in_2,
  input  in_3,
  output [7:0] out_4
);

  wire [7:0] d_ff_1_q;

  D_Flip_Flop #(.trigger("high")) d_ff_1 (.clk(in_1), .D(in_2[0]), .Q(d_ff_1_q[0]));  // open: Qn, preset, en, reset
  D_Flip_Flop #(.trigger("high")) d_ff_2 (.clk(in_1), .D(in_2[1]), .Q(d_ff_1_q[1]));  // open: Qn, preset, en, reset
  D_Flip_Flop #(.trigger("high")) d_ff_3 (.clk(in_1), .D(in_2[2]), .Q(d_ff_1_q[2]));  // open: Qn, preset, en, reset
  D_Flip_Flop #(.trigger("high")) d_ff_4 (.clk(in_1), .D(in_2[3]), .Q(d_ff_1_q[3]));  // open: Qn, preset, en, reset
  D_Flip_Flop #(.trigger("high")) d_ff_5 (.clk(in_1), .D(in_2[4]), .Q(d_ff_1_q[4]));  // open: Qn, preset, en, reset
  D_Flip_Flop #(.trigger("high")) d_ff_6 (.clk(in_1), .D(in_2[5]), .Q(d_ff_1_q[5]));  // open: Qn, preset, en, reset
  D_Flip_Flop #(.trigger("high")) d_ff_7 (.clk(in_1), .D(in_2[6]), .Q(d_ff_1_q[6]));  // open: Qn, preset, en, reset
  D_Flip_Flop #(.trigger("high")) d_ff_8 (.clk(in_1), .D(in_2[7]), .Q(d_ff_1_q[7]));  // open: Qn, preset, en, reset
  assign out_4 = in_3 ? d_ff_1_q : 8'bz;  // Controlled_Buffer controlled_buffer_1
endmodule

module low_register (
  input  in_1,
  input  [7:0] in_2,
  input  in_3,
  output [7:0] out_4
);

  wire [7:0] d_ff_1_q;

  D_Flip_Flop #(.trigger("low")) d_ff_1 (.clk(in_1), .D(in_2[0]), .Q(d_ff_1_q[0]));  // open: Qn, preset, en, reset
  D_Flip_Flop #(.trigger("low")) d_ff_2 (.clk(in_1), .D(in_2[1]), .Q(d_ff_1_q[1]));  // open: Qn, preset, en, reset
  D_Flip_Flop #(.trigger("low")) d_ff_3 (.clk(in_1), .D(in_2[2]), .Q(d_ff_1_q[2]));  // open: Qn, preset, en, reset
  D_Flip_Flop #(.trigger("low")) d_ff_4 (.clk(in_1), .D(in_2[3]), .Q(d_ff_1_q[3]));  // open: Qn, preset, en, reset
  D_Flip_Flop #(.trigger("low")) d_ff_5 (.clk(in_1), .D(in_2[4]), .Q(d_ff_1_q[4]));  // open: Qn, preset, en, reset
  D_Flip_Flop #(.trigger("low")) d_ff_6 (.clk(in_1), .D(in_2[5]), .Q(d_ff_1_q[5]));  // open: Qn, preset, en, reset
  D_Flip_Flop #(.trigger("low")) d_ff_7 (.clk(in_1), .D(in_2[6]), .Q(d_ff_1_q[6]));  // open: Qn, preset, en, reset
  D_Flip_Flop #(.trigger("low")) d_ff_8 (.clk(in_1), .D(in_2[7]), .Q(d_ff_1_q[7]));  // open: Qn, preset, en, reset
  assign out_4 = in_3 ? d_ff_1_q : 8'bz;  // Controlled_Buffer controlled_buffer_1
endmodule

module counter (
  input  clk,
  input  enable_chip,
  input  [15:0] in_3,
  input  reset,
  input  in_5,
  output [15:0] out_6
);

  wire and_1_out, d_ff_1_qn, d_ff_2_qn, d_ff_3_qn, d_ff_4_qn, d_ff_5_qn, d_ff_6_qn, d_ff_7_qn, d_ff_8_qn,
       d_ff_9_qn, d_ff_10_qn, d_ff_11_qn, d_ff_12_qn, d_ff_13_qn, d_ff_14_qn, d_ff_15_qn, d_ff_16_qn,
       multiplexer_1_out, multiplexer_2_out, multiplexer_3_out, multiplexer_4_out, multiplexer_5_out,
       multiplexer_6_out, multiplexer_7_out, multiplexer_8_out, multiplexer_9_out, multiplexer_10_out,
       multiplexer_11_out, multiplexer_12_out, multiplexer_13_out, multiplexer_14_out, multiplexer_15_out,
       multiplexer_16_out, multiplexer_17_out, multiplexer_18_out, multiplexer_19_out, multiplexer_20_out,
       multiplexer_21_out, multiplexer_22_out, multiplexer_23_out, multiplexer_24_out, multiplexer_25_out,
       multiplexer_26_out, multiplexer_27_out, multiplexer_28_out, multiplexer_29_out, multiplexer_30_out,
       multiplexer_31_out, multiplexer_32_out;

  and and_1 (and_1_out, clk, enable_chip);
  Multiplexer #(.enable("false")) multiplexer_1 (.in0(and_1_out), .in1(and_1_out), .out(multiplexer_1_out), .sel(in_5));
  Multiplexer #(.enable("false")) multiplexer_2 (.in0(in_3[0]), .in1(d_ff_1_qn), .out(multiplexer_2_out), .sel(in_5));
  Multiplexer #(.enable("false")) multiplexer_3 (.in0(and_1_out), .in1(out_6[0]), .out(multiplexer_3_out), .sel(in_5));
  Multiplexer #(.enable("false")) multiplexer_4 (.in0(in_3[1]), .in1(d_ff_2_qn), .out(multiplexer_4_out), .sel(in_5));
  Multiplexer #(.enable("false")) multiplexer_5 (.in0(and_1_out), .in1(out_6[1]), .out(multiplexer_5_out), .sel(in_5));
  Multiplexer #(.enable("false")) multiplexer_6 (.in0(in_3[2]), .in1(d_ff_3_qn), .out(multiplexer_6_out), .sel(in_5));
  Multiplexer #(.enable("false")) multiplexer_7 (.in0(and_1_out), .in1(out_6[2]), .out(multiplexer_7_out), .sel(in_5));
  Multiplexer #(.enable("false")) multiplexer_8 (.in0(in_3[3]), .in1(d_ff_4_qn), .out(multiplexer_8_out), .sel(in_5));
  Multiplexer #(.enable("false")) multiplexer_9 (.in0(and_1_out), .in1(out_6[3]), .out(multiplexer_9_out), .sel(in_5));
  Multiplexer #(.enable("false")) multiplexer_10 (.in0(in_3[4]), .in1(d_ff_5_qn), .out(multiplexer_10_out), .sel(in_5));
  Multiplexer #(.enable("false")) multiplexer_11 (
    .in0(and_1_out), .in1(out_6[4]), .out(multiplexer_11_out), .sel(in_5));
  Multiplexer #(.enable("false")) multiplexer_12 (.in0(in_3[5]), .in1(d_ff_6_qn), .out(multiplexer_12_out), .sel(in_5));
  Multiplexer #(.enable("false")) multiplexer_13 (
    .in0(and_1_out), .in1(out_6[5]), .out(multiplexer_13_out), .sel(in_5));
  Multiplexer #(.enable("false")) multiplexer_14 (.in0(in_3[6]), .in1(d_ff_7_qn), .out(multiplexer_14_out), .sel(in_5));
  Multiplexer #(.enable("false")) multiplexer_15 (
    .in0(and_1_out), .in1(out_6[6]), .out(multiplexer_15_out), .sel(in_5));
  Multiplexer #(.enable("false")) multiplexer_16 (.in0(in_3[7]), .in1(d_ff_8_qn), .out(multiplexer_16_out), .sel(in_5));
  Multiplexer #(.enable("false")) multiplexer_17 (
    .in0(and_1_out), .in1(out_6[7]), .out(multiplexer_17_out), .sel(in_5));
  Multiplexer #(.enable("false")) multiplexer_18 (.in0(in_3[8]), .in1(d_ff_9_qn), .out(multiplexer_18_out), .sel(in_5));
  Multiplexer #(.enable("false")) multiplexer_19 (
    .in0(and_1_out), .in1(out_6[8]), .out(multiplexer_19_out), .sel(in_5));
  Multiplexer #(.enable("false")) multiplexer_20 (
    .in0(in_3[9]), .in1(d_ff_10_qn), .out(multiplexer_20_out), .sel(in_5));
  Multiplexer #(.enable("false")) multiplexer_21 (
    .in0(and_1_out), .in1(out_6[9]), .out(multiplexer_21_out), .sel(in_5));
  Multiplexer #(.enable("false")) multiplexer_22 (
    .in0(in_3[10]), .in1(d_ff_11_qn), .out(multiplexer_22_out), .sel(in_5));
  Multiplexer #(.enable("false")) multiplexer_23 (
    .in0(and_1_out), .in1(out_6[10]), .out(multiplexer_23_out), .sel(in_5));
  Multiplexer #(.enable("false")) multiplexer_24 (
    .in0(in_3[11]), .in1(d_ff_12_qn), .out(multiplexer_24_out), .sel(in_5));
  Multiplexer #(.enable("false")) multiplexer_25 (
    .in0(and_1_out), .in1(out_6[11]), .out(multiplexer_25_out), .sel(in_5));
  Multiplexer #(.enable("false")) multiplexer_26 (
    .in0(in_3[12]), .in1(d_ff_13_qn), .out(multiplexer_26_out), .sel(in_5));
  Multiplexer #(.enable("false")) multiplexer_27 (
    .in0(and_1_out), .in1(out_6[12]), .out(multiplexer_27_out), .sel(in_5));
  Multiplexer #(.enable("false")) multiplexer_28 (
    .in0(in_3[13]), .in1(d_ff_14_qn), .out(multiplexer_28_out), .sel(in_5));
  Multiplexer #(.enable("false")) multiplexer_29 (
    .in0(and_1_out), .in1(out_6[13]), .out(multiplexer_29_out), .sel(in_5));
  Multiplexer #(.enable("false")) multiplexer_30 (
    .in0(in_3[14]), .in1(d_ff_15_qn), .out(multiplexer_30_out), .sel(in_5));
  Multiplexer #(.enable("false")) multiplexer_31 (
    .in0(and_1_out), .in1(out_6[14]), .out(multiplexer_31_out), .sel(in_5));
  Multiplexer #(.enable("false")) multiplexer_32 (
    .in0(in_3[15]), .in1(d_ff_16_qn), .out(multiplexer_32_out), .sel(in_5));
  D_Flip_Flop #(.trigger("falling")) d_ff_1 (
    .clk(multiplexer_1_out), .D(multiplexer_2_out), .Q(out_6[0]), .Qn(d_ff_1_qn), .reset(reset));  // open: preset, en
  D_Flip_Flop #(.trigger("falling")) d_ff_2 (
    .clk(multiplexer_3_out), .D(multiplexer_4_out), .Q(out_6[1]), .Qn(d_ff_2_qn), .reset(reset));  // open: preset, en
  D_Flip_Flop #(.trigger("falling")) d_ff_3 (
    .clk(multiplexer_5_out), .D(multiplexer_6_out), .Q(out_6[2]), .Qn(d_ff_3_qn), .reset(reset));  // open: preset, en
  D_Flip_Flop #(.trigger("falling")) d_ff_4 (
    .clk(multiplexer_7_out), .D(multiplexer_8_out), .Q(out_6[3]), .Qn(d_ff_4_qn), .reset(reset));  // open: preset, en
  D_Flip_Flop #(.trigger("falling")) d_ff_5 (
    .clk(multiplexer_9_out), .D(multiplexer_10_out), .Q(out_6[4]), .Qn(d_ff_5_qn), .reset(reset));  // open: preset, en
  D_Flip_Flop #(.trigger("falling")) d_ff_6 (
    .clk(multiplexer_11_out), .D(multiplexer_12_out), .Q(out_6[5]), .Qn(d_ff_6_qn), .reset(reset));  // open: preset, en
  D_Flip_Flop #(.trigger("falling")) d_ff_7 (
    .clk(multiplexer_13_out), .D(multiplexer_14_out), .Q(out_6[6]), .Qn(d_ff_7_qn), .reset(reset));  // open: preset, en
  D_Flip_Flop #(.trigger("falling")) d_ff_8 (
    .clk(multiplexer_15_out), .D(multiplexer_16_out), .Q(out_6[7]), .Qn(d_ff_8_qn), .reset(reset));  // open: preset, en
  D_Flip_Flop #(.trigger("falling")) d_ff_9 (
    .clk(multiplexer_17_out), .D(multiplexer_18_out), .Q(out_6[8]), .Qn(d_ff_9_qn), .reset(reset));  // open: preset, en
  D_Flip_Flop #(.trigger("falling")) d_ff_10 (
    .clk(multiplexer_19_out), .D(multiplexer_20_out), .Q(out_6[9]), .Qn(d_ff_10_qn), .reset(reset));  // open: preset, en
  D_Flip_Flop #(.trigger("falling")) d_ff_11 (
    .clk(multiplexer_21_out), .D(multiplexer_22_out), .Q(out_6[10]), .Qn(d_ff_11_qn), .reset(reset));  // open: preset, en
  D_Flip_Flop #(.trigger("falling")) d_ff_12 (
    .clk(multiplexer_23_out), .D(multiplexer_24_out), .Q(out_6[11]), .Qn(d_ff_12_qn), .reset(reset));  // open: preset, en
  D_Flip_Flop #(.trigger("falling")) d_ff_13 (
    .clk(multiplexer_25_out), .D(multiplexer_26_out), .Q(out_6[12]), .Qn(d_ff_13_qn), .reset(reset));  // open: preset, en
  D_Flip_Flop #(.trigger("falling")) d_ff_14 (
    .clk(multiplexer_27_out), .D(multiplexer_28_out), .Q(out_6[13]), .Qn(d_ff_14_qn), .reset(reset));  // open: preset, en
  D_Flip_Flop #(.trigger("falling")) d_ff_15 (
    .clk(multiplexer_29_out), .D(multiplexer_30_out), .Q(out_6[14]), .Qn(d_ff_15_qn), .reset(reset));  // open: preset, en
  D_Flip_Flop #(.trigger("falling")) d_ff_16 (
    .clk(multiplexer_31_out), .D(multiplexer_32_out), .Q(out_6[15]), .Qn(d_ff_16_qn), .reset(reset));  // open: preset, en

  // Notes on the sheet:
  //   inp_en/count
endmodule
